# Fritzing sketch UGV (saved by Fritzing 0.7.10b)
breadboards: 1

parts:
  LCD1 = LCD screen [part_number=lcd]
  U1 = Voltage Regulator - 5V [part_number=L7805CV package="TO220 [THT]"]
  IC1 = IC, DIP package, 16 pins [chip_label=L293D]
  Arduino1 = Arduino  # not connected
  U2 = XBee
  Εξάρτημα1 = Arduino Wireless SD Shield
  U3 = XBee
  VCC1 = Battery block 9V  # not connected
  M1 = DC Motor
  M2 = DC Motor
  J1 = Basic Servo
  J2 = Infrared Proximity Sensor
  R2 = Rotary Potentiometer (Small) [maximum_resistance=100kΩ]
  R3 = Resistor [tolerance=±5% resistance=220 package=THT]
  VCC2 = 4 x AAA Battery Mount

nets:
  GND: LCD1.VSS, LCD1.R/W, Εξάρτημα1.GND, J1.gnd, J2.GND, R2.leg2
  VCC: LCD1.VDD, Εξάρτημα1.+5V, J1.vcc, J2.Vcc, R2.leg1
  N1: LCD1.RS, Εξάρτημα1.D12
  N2: LCD1.E, Εξάρτημα1.D11
  N3: LCD1.DB4, Εξάρτημα1.D5
  N4: LCD1.DB5, Εξάρτημα1.SD_CS
  N5: LCD1.DB6, Εξάρτημα1.D3
  N6: LCD1.DB7, Εξάρτημα1.D2
  N7: LCD1.LED+, R3.Pin_0
  N8: LCD1.LED-, U1.GND, IC1.pin4, IC1.pin5, IC1.pin12, IC1.pin13, VCC2.-
  N9: U1.input_voltage, IC1.pin1, IC1.pin8, IC1.pin9, IC1.pin16, VCC2.+
  N10: U1.output_voltage, R3.Pin_1
  N11: IC1.pin2, Εξάρτημα1.D9
  N12: IC1.pin3, M1.pin_1
  N13: IC1.pin6, M1.pin_2
  N14: IC1.pin7, Εξάρτημα1.D8
  N15: IC1.pin10, Εξάρτημα1.D6
  N16: IC1.pin11, M2.pin_1
  N17: IC1.pin14, M2.pin_2
  N18: IC1.pin15, Εξάρτημα1.D7
  GND_2: U2.GND, Εξάρτημα1.N$92, U3.GND
  N19: U2.pin11, Εξάρτημα1.N$122, U3.pin11
  N20: Εξάρτημα1.A0, J2.Vout
  N21: Εξάρτημα1.D10, J1.pulse
